// Logisim project CSE332.8-2111090642-Benzamin Yasir Siam-LAB9.circ as structural Verilog: 7 circuits, main circuit SINGLE CYCLE DATAPATH FOR R-TYPE & I-TYPE INSTRUCTIONS
module SINGLE_CYCLE_DATAPATH_FOR_R_TYPE___I_TYPE_INSTRUCTIONS (
  input  Cin,
  input  CLEAR,
  output Cout
);

  wire CLK, main_control_1_alusrc, main_control_1_mem_read, main_control_1_mem_write,
       main_control_1_memtoreg, main_control_1_regdst, main_control_1_write_control;
  wire [1:0] multiplexer_2_out;
  wire [2:0] multiplexer_1_out;
  wire [3:0] adder_1_out, bit_extender_1_out, multiplexer_3_out, multiplexer_4_out, n4_bit_alu_1_result,
       n4_bit_register_file_1_read_data_1, n4_bit_register_file_1_read_data_2, ram_1_data, register_1_q;
  wire [11:0] rom_1_data;

  Register #(.width(4)) register_1 (.D(adder_1_out), .Q(register_1_q), .clk(CLK), .clr(CLEAR));  // open: en
  Clock CLOCK (.out(CLK));
  Adder #(.width(4)) adder_1 (.a(register_1_q), .b(4'b0001), .out(adder_1_out));  // open: cin, cout
  ROM #(.addrWidth(4), .dataWidth(12)) rom_1 (.addr(register_1_q), .data(rom_1_data));  // open: sel
  Main_Control main_control_1 (
    .WRITE_CONTROL(main_control_1_write_control), .ALUsrc(main_control_1_alusrc), .OP_CODE(rom_1_data[11:9]),
    .MEM_READ(main_control_1_mem_read), .MEM_WRITE(main_control_1_mem_write),
    .MEMtoREG(main_control_1_memtoreg), .REGdst(main_control_1_regdst));
  Multiplexer #(.width(3), .enable("false")) multiplexer_1 (
    .in0(rom_1_data[5:3]), .in1(rom_1_data[2:0]), .out(multiplexer_1_out), .sel(main_control_1_regdst));
  Multiplexer #(.width(2), .enable("false")) multiplexer_2 (
    .in0(rom_1_data[10:9]), .in1(2'b10), .out(multiplexer_2_out), .sel(rom_1_data[11]));
  _4_BIT_REGISTER_FILE u_4_bit_register_file_1 (
    .WRITE_REGISTER(multiplexer_1_out), .WRITE_DATA(multiplexer_4_out),
    .READ_DATA_1(n4_bit_register_file_1_read_data_1), .READ_REGISTER_1(rom_1_data[8:6]),
    .READ_DATA_2(n4_bit_register_file_1_read_data_2), .READ_REGISTER_2(rom_1_data[5:3]),
    .WRITE_CONTROL_PIN(main_control_1_write_control), .CLOCK(CLK));
  assign bit_extender_1_out = {{1{1'b0}}, rom_1_data[2:0]};  // Bit_Extender bit_extender_1
  Multiplexer #(.width(4), .enable("false")) multiplexer_3 (
    .in0(n4_bit_register_file_1_read_data_2), .in1(bit_extender_1_out), .out(multiplexer_3_out),
    .sel(main_control_1_alusrc));
  _4_BIT_ALU u_4_bit_alu_1 (
    .A(n4_bit_register_file_1_read_data_1), .B(multiplexer_3_out), .RESULT(n4_bit_alu_1_result), .Cout(Cout),
    .Cin(Cin), .SELECT_BITS(multiplexer_2_out));
  Multiplexer #(.width(4), .enable("false")) multiplexer_4 (
    .in0(n4_bit_alu_1_result), .in1(ram_1_data), .out(multiplexer_4_out), .sel(main_control_1_memtoreg));
  RAM #(.addrWidth(4), .dataWidth(4), .bus("separate")) ram_1 (
    .addr(n4_bit_alu_1_result), .din(n4_bit_register_file_1_read_data_2), .data(ram_1_data),
    .str(main_control_1_mem_write), .clk(CLK), .ld(main_control_1_mem_read));  // open: sel, clr

  // Notes on the sheet:
  //   contents of rom_1 (hex, n*v repeats v):
  //   8ea 88e 66b a9c
endmodule

module SINGLE_CYCLE_DATAPATH_FOR_R_TYPE_INSTRUCTIONS (
  input  Cin,
  input  CLEAR,
  input  in_3,
  output Cout
);

  wire clock_1_out;
  wire [3:0] adder_1_out, n4_bit_alu_1_result, n4_bit_register_file_1_read_data_1,
       n4_bit_register_file_1_read_data_2, register_1_q;
  wire [10:0] rom_1_data;

  Register #(.width(4)) register_1 (.D(adder_1_out), .Q(register_1_q), .clk(clock_1_out), .clr(CLEAR));  // open: en
  Adder #(.width(4)) adder_1 (.a(register_1_q), .b(4'b0001), .out(adder_1_out));  // open: cin, cout
  ROM #(.addrWidth(4), .dataWidth(11)) rom_1 (.addr(register_1_q), .data(rom_1_data));  // open: sel
  Clock clock_1 (.out(clock_1_out));
  _4_BIT_REGISTER_FILE u_4_bit_register_file_1 (
    .WRITE_REGISTER(rom_1_data[2:0]), .WRITE_DATA(n4_bit_alu_1_result),
    .READ_DATA_1(n4_bit_register_file_1_read_data_1), .READ_REGISTER_1(rom_1_data[8:6]),
    .READ_DATA_2(n4_bit_register_file_1_read_data_2), .READ_REGISTER_2(rom_1_data[5:3]),
    .WRITE_CONTROL_PIN(in_3), .CLOCK(clock_1_out));
  _4_BIT_ALU u_4_bit_alu_1 (
    .A(n4_bit_register_file_1_read_data_1), .B(n4_bit_register_file_1_read_data_2),
    .RESULT(n4_bit_alu_1_result), .Cout(Cout), .Cin(Cin), .SELECT_BITS(rom_1_data[10:9]));

  // Notes on the sheet:
  //   contents of rom_1 (hex, n*v repeats v):
  //   40c 9d 72f
endmodule

module SINGLE_CYCLE_DATAPATH_FOR_I_TYPE_INSTRUCTIONS (
  input  Cin,
  input  CLEAR,
  input  MEM_WRITE,
  input  MEM_READ,
  input  in_5,
  output Cout
);

  wire clock_1_out;
  wire [3:0] adder_1_out, bit_extender_1_out, n4_bit_alu_1_result, n4_bit_register_file_1_read_data_1,
       n4_bit_register_file_1_read_data_2, ram_1_data, register_1_q;
  wire [11:0] rom_1_data;

  Register #(.width(4)) register_1 (.D(adder_1_out), .Q(register_1_q), .clk(clock_1_out), .clr(CLEAR));  // open: en
  Clock clock_1 (.out(clock_1_out));
  Adder #(.width(4)) adder_1 (.a(register_1_q), .b(4'b0001), .out(adder_1_out));  // open: cin, cout
  ROM #(.addrWidth(4), .dataWidth(12)) rom_1 (.addr(register_1_q), .data(rom_1_data));  // open: sel
  _4_BIT_REGISTER_FILE u_4_bit_register_file_1 (
    .WRITE_REGISTER(rom_1_data[5:3]), .WRITE_DATA(ram_1_data),
    .READ_DATA_1(n4_bit_register_file_1_read_data_1), .READ_REGISTER_1(rom_1_data[8:6]),
    .READ_DATA_2(n4_bit_register_file_1_read_data_2), .READ_REGISTER_2(rom_1_data[5:3]),
    .WRITE_CONTROL_PIN(in_5), .CLOCK(clock_1_out));
  assign bit_extender_1_out = {{1{1'b0}}, rom_1_data[2:0]};  // Bit_Extender bit_extender_1
  _4_BIT_ALU u_4_bit_alu_1 (
    .A(n4_bit_register_file_1_read_data_1), .B(bit_extender_1_out), .RESULT(n4_bit_alu_1_result),
    .Cout(Cout), .Cin(Cin), .SELECT_BITS(rom_1_data[11:10]));
  RAM #(.addrWidth(4), .dataWidth(4), .bus("separate")) ram_1 (
    .addr(n4_bit_alu_1_result), .din(n4_bit_register_file_1_read_data_2), .data(ram_1_data), .str(MEM_WRITE),
    .clk(clock_1_out), .ld(MEM_READ));  // open: sel, clr

  // Notes on the sheet:
  //   contents of rom_1 (hex, n*v repeats v):
  //   863 86f aaa
endmodule

module Main_Control (
  input  [2:0] OP_CODE,
  output WRITE_CONTROL,
  output REGdst,
  output ALUsrc,
  output MEM_READ,
  output MEM_WRITE,
  output MEMtoREG
);

  wire decoder_1_out0, decoder_1_out1, decoder_1_out2, decoder_1_out3;

  Decoder #(.select(3), .enable("false")) decoder_1 (
    .out0(decoder_1_out0), .out1(decoder_1_out1), .out2(decoder_1_out2), .out3(decoder_1_out3),
    .out4(MEM_READ), .out5(MEM_WRITE), .sel(OP_CODE));  // open: out6, out7
  or or_1 (ALUsrc, MEM_READ, MEM_WRITE);
  or or_2 (WRITE_CONTROL, decoder_1_out0, decoder_1_out1, decoder_1_out2, decoder_1_out3, MEM_READ);
  or or_3 (REGdst, decoder_1_out0, decoder_1_out1, decoder_1_out2, decoder_1_out3);

  assign MEMtoREG = MEM_READ;
endmodule

module _4_BIT_REGISTER_FILE (
  input  CLOCK,
  input  WRITE_CONTROL_PIN,
  input  [2:0] WRITE_REGISTER,
  input  [2:0] READ_REGISTER_1,
  input  [3:0] WRITE_DATA,
  input  [2:0] READ_REGISTER_2,
  output [3:0] READ_DATA_1,
  output [3:0] READ_DATA_2
);

  wire and_1_out, decoder_1_out0, decoder_1_out1, decoder_1_out2, decoder_1_out3, decoder_1_out4,
       decoder_1_out5, decoder_1_out6, decoder_1_out7;
  wire [3:0] register_1_q, register_2_q, register_3_q, register_4_q, register_5_q, register_6_q,
       register_7_q, register_8_q;

  Decoder #(.select(3), .enable("false")) decoder_1 (
    .out0(decoder_1_out0), .out1(decoder_1_out1), .out2(decoder_1_out2), .out3(decoder_1_out3),
    .out4(decoder_1_out4), .out5(decoder_1_out5), .out6(decoder_1_out6), .out7(decoder_1_out7),
    .sel(WRITE_REGISTER));
  and and_1 (and_1_out, CLOCK, WRITE_CONTROL_PIN);
  Register #(.width(4)) register_1 (
    .D(WRITE_DATA), .en(decoder_1_out0), .Q(register_1_q), .clk(and_1_out));  // open: clr
  Register #(.width(4)) register_2 (
    .D(WRITE_DATA), .en(decoder_1_out1), .Q(register_2_q), .clk(and_1_out));  // open: clr
  Register #(.width(4)) register_3 (
    .D(WRITE_DATA), .en(decoder_1_out2), .Q(register_3_q), .clk(and_1_out));  // open: clr
  Register #(.width(4)) register_4 (
    .D(WRITE_DATA), .en(decoder_1_out3), .Q(register_4_q), .clk(and_1_out));  // open: clr
  Register #(.width(4)) register_5 (
    .D(WRITE_DATA), .en(decoder_1_out4), .Q(register_5_q), .clk(and_1_out));  // open: clr
  Register #(.width(4)) register_6 (
    .D(WRITE_DATA), .en(decoder_1_out5), .Q(register_6_q), .clk(and_1_out));  // open: clr
  Register #(.width(4)) register_7 (
    .D(WRITE_DATA), .en(decoder_1_out6), .Q(register_7_q), .clk(and_1_out));  // open: clr
  Register #(.width(4)) register_8 (
    .D(WRITE_DATA), .en(decoder_1_out7), .Q(register_8_q), .clk(and_1_out));  // open: clr
  Multiplexer #(.select(3), .width(4), .enable("false")) multiplexer_1 (
    .in0(register_1_q), .in1(register_2_q), .in2(register_3_q), .in3(register_4_q), .in4(register_5_q),
    .in5(register_6_q), .in6(register_7_q), .in7(register_8_q), .out(READ_DATA_1), .sel(READ_REGISTER_1));
  Multiplexer #(.select(3), .width(4), .enable("false")) multiplexer_2 (
    .in0(register_1_q), .in1(register_2_q), .in2(register_3_q), .in3(register_4_q), .in4(register_5_q),
    .in5(register_6_q), .in6(register_7_q), .in7(register_8_q), .out(READ_DATA_2), .sel(READ_REGISTER_2));
endmodule

module _1_BIT_ALU (
  input  A,
  input  B,
  input  Cin,
  input  [1:0] SELECT_BITS,
  output RESULT,
  output Cout
);

  wire adder_1_cout, adder_1_out, and_1_out, or_1_out, subtractor_1_bout, subtractor_1_out;

  and and_1 (and_1_out, A, B);
  or or_1 (or_1_out, A, B);
  Adder #(.width(1)) adder_1 (.a(A), .b(B), .out(adder_1_out), .cin(Cin), .cout(adder_1_cout));
  Subtractor #(.width(1)) subtractor_1 (.a(A), .b(B), .out(subtractor_1_out), .bin(Cin), .bout(subtractor_1_bout));
  Multiplexer #(.select(2), .enable("false")) multiplexer_1 (
    .in0(and_1_out), .in1(or_1_out), .in2(adder_1_out), .in3(subtractor_1_out), .out(RESULT),
    .sel(SELECT_BITS));
  Multiplexer multiplexer_2 (
    .in0(adder_1_cout), .in1(subtractor_1_bout), .out(Cout), .sel(SELECT_BITS[0]), .en(SELECT_BITS[1]));
endmodule

module _4_BIT_ALU (
  input  Cin,
  input  [3:0] A,
  input  [3:0] B,
  input  [1:0] SELECT_BITS,
  output [3:0] RESULT,
  output Cout
);

  wire n1_bit_alu_1_cout, n1_bit_alu_2_cout, n1_bit_alu_3_cout;

  _1_BIT_ALU u_1_bit_alu_1 (
    .RESULT(RESULT[0]), .SELECT_BITS(SELECT_BITS), .Cout(n1_bit_alu_1_cout), .A(A[0]), .B(B[0]), .Cin(Cin));
  _1_BIT_ALU u_1_bit_alu_2 (
    .RESULT(RESULT[1]), .SELECT_BITS(SELECT_BITS), .Cout(n1_bit_alu_2_cout), .A(A[1]), .B(B[1]),
    .Cin(n1_bit_alu_1_cout));
  _1_BIT_ALU u_1_bit_alu_3 (
    .RESULT(RESULT[2]), .SELECT_BITS(SELECT_BITS), .Cout(n1_bit_alu_3_cout), .A(A[2]), .B(B[2]),
    .Cin(n1_bit_alu_2_cout));
  _1_BIT_ALU u_1_bit_alu_4 (
    .RESULT(RESULT[3]), .SELECT_BITS(SELECT_BITS), .Cout(Cout), .A(A[3]), .B(B[3]), .Cin(n1_bit_alu_3_cout));

  // Notes on the sheet:
  //   0
  //   1
  //   2
  //   3
endmodule
