// Logisim project CSE332L.8-2111090642-Benzamin Yasir Siam-Final.circ as structural Verilog: 3 circuits, main circuit main
module main (
  input  CLEAR,
  input  in_2,
  output out_3
);

  wire CLOCK_out;
  wire [3:0] adder_1_out, register_1_q;
  wire [7:0] alu_1_result, n8_bit_register_1_read_a, n8_bit_register_1_read_b;
  wire [11:0] rom_1_data;

  Register #(.width(4)) register_1 (.D(adder_1_out), .Q(register_1_q), .clk(CLOCK_out), .clr(CLEAR));  // open: en
  Clock CLOCK (.out(CLOCK_out));
  Adder #(.width(4)) adder_1 (.a(4'b0001), .b(register_1_q), .out(adder_1_out));  // open: cin, cout
  ROM #(.addrWidth(4), .dataWidth(12)) rom_1 (.addr(register_1_q), .data(rom_1_data));  // open: sel
  _8_bit_Register u_8_bit_register_1 (
    .Data_In(alu_1_result), .Write_Enable(in_2), .Read_A(n8_bit_register_1_read_a),
    .Read_B(n8_bit_register_1_read_b), .Write_Address(rom_1_data[2:0]), .CLK(CLOCK_out),
    .Address_A(rom_1_data[8:6]), .Address_B(rom_1_data[5:3]));
  ALU alu_1 (
    .Operand_A(n8_bit_register_1_read_a), .Operand_B(n8_bit_register_1_read_b), .Zero_Flag(out_3),
    .Result(alu_1_result), .ALUOp(rom_1_data[11:9]));

  // Notes on the sheet:
  //   contents of rom_1 (hex, n*v repeats v):
  //   411 2ec
endmodule

module _8_bit_Register (
  input  [7:0] Data_In,
  input  Write_Enable,
  input  [2:0] Address_A,
  input  [2:0] Write_Address,
  input  [2:0] Address_B,
  input  CLK,
  output [7:0] Read_A,
  output [7:0] Read_B
);

  wire and_1_out, and_2_out, and_3_out, and_4_out, and_5_out, and_6_out, and_7_out, and_8_out,
       decoder_1_out0, decoder_1_out1, decoder_1_out2, decoder_1_out3, decoder_1_out4, decoder_1_out5,
       decoder_1_out6, decoder_1_out7;
  wire [7:0] register_1_q, register_2_q, register_3_q, register_4_q, register_5_q, register_6_q,
       register_7_q, register_8_q;

  Decoder #(.select(3)) decoder_1 (
    .out0(decoder_1_out0), .out1(decoder_1_out1), .out2(decoder_1_out2), .out3(decoder_1_out3),
    .out4(decoder_1_out4), .out5(decoder_1_out5), .out6(decoder_1_out6), .out7(decoder_1_out7),
    .sel(Write_Address));  // open: en
  and and_1 (and_1_out, decoder_1_out0, Write_Enable);
  and and_2 (and_2_out, decoder_1_out1, Write_Enable);
  and and_3 (and_3_out, decoder_1_out2, Write_Enable);
  and and_4 (and_4_out, decoder_1_out3, Write_Enable);
  and and_5 (and_5_out, decoder_1_out4, Write_Enable);
  and and_6 (and_6_out, decoder_1_out5, Write_Enable);
  and and_7 (and_7_out, decoder_1_out6, Write_Enable);
  and and_8 (and_8_out, decoder_1_out7, Write_Enable);
  Register register_1 (.D(Data_In), .en(and_1_out), .Q(register_1_q), .clk(CLK));  // open: clr
  Register register_2 (.D(Data_In), .en(and_2_out), .Q(register_2_q), .clk(CLK));  // open: clr
  Register register_3 (.D(Data_In), .en(and_3_out), .Q(register_3_q), .clk(CLK));  // open: clr
  Register register_4 (.D(Data_In), .en(and_4_out), .Q(register_4_q), .clk(CLK));  // open: clr
  Register register_5 (.D(Data_In), .en(and_5_out), .Q(register_5_q), .clk(CLK));  // open: clr
  Register register_6 (.D(Data_In), .en(and_6_out), .Q(register_6_q), .clk(CLK));  // open: clr
  Register register_7 (.D(Data_In), .en(and_7_out), .Q(register_7_q), .clk(CLK));  // open: clr
  Register register_8 (.D(Data_In), .en(and_8_out), .Q(register_8_q), .clk(CLK));  // open: clr
  Multiplexer #(.select(3), .width(8)) multiplexer_1 (
    .in0(register_1_q), .in1(register_2_q), .in2(register_3_q), .in3(register_4_q), .in4(register_5_q),
    .in5(register_6_q), .in6(register_7_q), .in7(register_8_q), .out(Read_A), .sel(Address_A));  // open: en
  Multiplexer #(.select(3), .width(8)) multiplexer_2 (
    .in0(register_1_q), .in1(register_2_q), .in2(register_3_q), .in3(register_4_q), .in4(register_5_q),
    .in5(register_6_q), .in6(register_7_q), .in7(register_8_q), .out(Read_B), .sel(Address_B));  // open: en
endmodule

module ALU (
  input  [7:0] Operand_A,
  input  [7:0] Operand_B,
  input  [2:0] ALUOp,
  output Zero_Flag,
  output [7:0] Result
);

  wire [7:0] adder_1_out, and_1_out, multiplier_1_out, nor_1_out, not_1_out, or_1_out, subtractor_1_out,
       xor_1_out;

  assign and_1_out = Operand_A & Operand_B;  // AND_Gate and_1, 8 bits wide
  Adder adder_1 (.a(Operand_A), .b(Operand_B), .out(adder_1_out));  // open: cin, cout
  assign or_1_out = Operand_A | Operand_B;  // OR_Gate or_1, 8 bits wide
  assign xor_1_out = Operand_A ^ Operand_B;  // XOR_Gate xor_1, 8 bits wide
  assign not_1_out = ~Operand_A;  // NOT_Gate not_1, 8 bits wide
  Subtractor subtractor_1 (.a(Operand_A), .b(Operand_B), .out(subtractor_1_out));  // open: bin, bout
  Multiplier multiplier_1 (.a(Operand_A), .b(Operand_B), .out(multiplier_1_out));  // open: cin, cout
  assign nor_1_out = ~(Operand_A | Operand_B);  // NOR_Gate nor_1, 8 bits wide
  Multiplexer #(.select(3), .width(8)) multiplexer_1 (
    .in0(and_1_out), .in1(adder_1_out), .in2(or_1_out), .in3(xor_1_out), .in4(not_1_out),
    .in5(subtractor_1_out), .in6(multiplier_1_out), .in7(nor_1_out), .out(Result), .sel(ALUOp));  // open: en
  nor nor_2 (Zero_Flag, Result[0], Result[1], Result[2], Result[3], Result[4], Result[5], Result[6], Result[7]);
endmodule
