// Logisim project LAB5-Design a 4-bit Register File-1.circ as structural Verilog: 2 circuits, main circuit MAIN
module MAIN (
  input  [2:0] in_1,
  input  [2:0] in_2,
  input  [2:0] in_3,
  input  [3:0] in_4,
  input  in_5,
  output [3:0] out_6,
  output [3:0] out_7
);

  wire clock_1_out;

  Clock clock_1 (.out(clock_1_out));
  _4_BIT_REGISTER_FILE u_4_bit_register_file_1 (
    .WRITE_REGISTER(in_3), .WRITE_DATA(in_4), .READ_DATA_1(out_6), .READ_REGISTER_1(in_1),
    .READ_DATA_2(out_7), .READ_REGISTER_2(in_2), .WRITE_CONTROL_PIN(in_5), .CLOCK(clock_1_out));

  // Notes on the sheet:
  //   BENZAMIN YASIR SIAM
  //   2111090642
endmodule

module _4_BIT_REGISTER_FILE (
  input  CLOCK,
  input  WRITE_CONTROL_PIN,
  input  [2:0] WRITE_REGISTER,
  input  [2:0] READ_REGISTER_1,
  input  [3:0] WRITE_DATA,
  input  [2:0] READ_REGISTER_2,
  output [3:0] READ_DATA_1,
  output [3:0] READ_DATA_2
);

  wire and_1_out, decoder_1_out0, decoder_1_out1, decoder_1_out2, decoder_1_out3, decoder_1_out4,
       decoder_1_out5, decoder_1_out6, decoder_1_out7;
  wire [3:0] register_1_q, register_2_q, register_3_q, register_4_q, register_5_q, register_6_q,
       register_7_q, register_8_q;

  Decoder #(.select(3), .enable("false")) decoder_1 (
    .out0(decoder_1_out0), .out1(decoder_1_out1), .out2(decoder_1_out2), .out3(decoder_1_out3),
    .out4(decoder_1_out4), .out5(decoder_1_out5), .out6(decoder_1_out6), .out7(decoder_1_out7),
    .sel(WRITE_REGISTER));
  and and_1 (and_1_out, CLOCK, WRITE_CONTROL_PIN);
  Register #(.width(4)) register_1 (
    .D(WRITE_DATA), .en(decoder_1_out0), .Q(register_1_q), .clk(and_1_out));  // open: clr
  Register #(.width(4)) register_2 (
    .D(WRITE_DATA), .en(decoder_1_out1), .Q(register_2_q), .clk(and_1_out));  // open: clr
  Register #(.width(4)) register_3 (
    .D(WRITE_DATA), .en(decoder_1_out2), .Q(register_3_q), .clk(and_1_out));  // open: clr
  Register #(.width(4)) register_4 (
    .D(WRITE_DATA), .en(decoder_1_out3), .Q(register_4_q), .clk(and_1_out));  // open: clr
  Register #(.width(4)) register_5 (
    .D(WRITE_DATA), .en(decoder_1_out4), .Q(register_5_q), .clk(and_1_out));  // open: clr
  Register #(.width(4)) register_6 (
    .D(WRITE_DATA), .en(decoder_1_out5), .Q(register_6_q), .clk(and_1_out));  // open: clr
  Register #(.width(4)) register_7 (
    .D(WRITE_DATA), .en(decoder_1_out6), .Q(register_7_q), .clk(and_1_out));  // open: clr
  Register #(.width(4)) register_8 (
    .D(WRITE_DATA), .en(decoder_1_out7), .Q(register_8_q), .clk(and_1_out));  // open: clr
  Multiplexer #(.select(3), .width(4), .enable("false")) multiplexer_1 (
    .in0(register_1_q), .in1(register_2_q), .in2(register_3_q), .in3(register_4_q), .in4(register_5_q),
    .in5(register_6_q), .in6(register_7_q), .in7(register_8_q), .out(READ_DATA_1), .sel(READ_REGISTER_1));
  Multiplexer #(.select(3), .width(4), .enable("false")) multiplexer_2 (
    .in0(register_1_q), .in1(register_2_q), .in2(register_3_q), .in3(register_4_q), .in4(register_5_q),
    .in5(register_6_q), .in6(register_7_q), .in7(register_8_q), .out(READ_DATA_2), .sel(READ_REGISTER_2));

  // Notes on the sheet:
  //   BENZAMIN YASIR SIAM
  //   2111090642
endmodule
